// Logisim project circuit_16_bit.circ as structural Verilog: 1 circuit, main circuit main
module main (
  input  RST,
  input  [15:0] INPUT
);

  wire and_1_out, CLK_out, not_1_out;
  wire [14:0] W1_q;
  wire [15:0] adder_1_out, adder_2_out, adder_3_out, adder_4_out, adder_5_out, adder_6_out, multiplier_1_out,
       multiplier_2_out, register_1_q, W2_q;
  wire [15:1] W3_q;
  wire [15:15] W1_q_2, W3_q_2;

  Clock CLK (.out(CLK_out));
  and and_1 (and_1_out, CLK_out, RST);
  Register #(.width(16)) register_1 (.D(INPUT), .en(1'b1), .Q(register_1_q), .clk(CLK_out), .clr(and_1_out));
  Register #(.width(16)) W1 (.D(adder_3_out), .en(1'b1), .Q({W1_q_2[15], W1_q}), .clk(CLK_out), .clr(and_1_out));
  Multiplier #(.width(16)) multiplier_1 (.a({W1_q, 1'b0}), .b(16'h7), .out(multiplier_1_out));  // open: cin, cout
  Register #(.width(16)) W2 (.D({W1_q_2[15], W1_q}), .en(1'b1), .Q(W2_q), .clk(CLK_out), .clr(and_1_out));
  Adder #(.width(16)) adder_1 (.a(multiplier_1_out), .b(register_1_q), .out(adder_1_out));  // open: cin, cout
  Register #(.width(16)) W3 (.D(W2_q), .en(1'b1), .Q({W3_q_2[15], W3_q}), .clk(CLK_out), .clr(and_1_out));
  Multiplier #(.width(16)) multiplier_2 (.a(W2_q), .b(16'hfffb), .out(multiplier_2_out));  // open: cin, cout
  Adder #(.width(16)) adder_2 (.a({W3_q, 1'b0}), .b(multiplier_2_out), .out(adder_2_out));  // open: cin, cout
  Adder #(.width(16)) adder_3 (.a(adder_2_out), .b(adder_1_out), .out(adder_3_out));  // open: cin, cout
  Adder #(.width(16)) adder_4 (.a({W3_q_2[15], W3_q}), .b(W2_q), .out(adder_4_out));  // open: cin, cout
  Adder #(.width(16)) adder_5 (.a(adder_4_out), .b(adder_6_out), .out(adder_5_out));  // open: cin, cout
  Adder #(.width(16)) adder_6 (.a({W1_q_2[15], W1_q}), .b(adder_3_out), .out(adder_6_out));  // open: cin, cout
  // Probe on {adder_5_out[14:0], 1'b0}
  // Probe on not_1_out
  not not_1 (not_1_out, RST);
endmodule
